# Fritzing sketch ESP32-Bluetooth-Speaker (saved by Fritzing 0.9.6b)
circuit board: 7.5cm x 5.2cm
breadboards: 1

parts:
  M1 = DOIT Esp32 DevKit v1 (30 pins long, 11 pins width) [part_number=ESP32S-PIN30]
  元件1 = Adafruit MAX98357A I2S 3W Class D Amplifier [part_number="Adafruit #3006"]
  元件2 = Adafruit MAX98357A I2S 3W Class D Amplifier [part_number="Adafruit #3006"]
  RE2 = Rotary Encoder [package=THT]
  R2 = Resistor [tolerance=±5% resistance=220 package="2512 [SMD]"]
  R1 = Resistor [tolerance=±10% resistance=220k package="1206 [SMD]"]
  LED1 = LED - 3mm [color="Blue (430nm)" current=0.030 package="3 mm [THT]"]

nets:
  N1: M1.D35, RE2.EncoderPinB
  N2: M1.D32, RE2.EncoderPinA
  N3: M1.D33, 元件1.DIN, 元件2.DIN
  N4: M1.D25, 元件1.BCLK, 元件2.BCLK
  N5: M1.D26, 元件1.LRCLK, 元件2.LRCLK
  N6: M1.D14, RE2.SwitchrPinD
  N7: M1.D13, 元件1.SD_MODE, R2.Pin_1, R1.Pin_1
  GND: M1.GND, 元件1.GND, 元件1.GAIN, 元件2.GND, 元件2.GAIN, RE2.EncoderPinC, RE2.SwitchPinE, LED1.cathode
  5V: M1.VIN, 元件1.VIN, 元件2.VIN
  N8: 元件2.SD_MODE, R1.Pin_0
  N9: R2.Pin_0, LED1.anode

custom parts:
  DOIT Esp32 DevKit v1 (30 pins long, 11 pins width): The DOIT Esp32 DevKit v1 is one of the development board created by DOIT to evaluate the ESP-WROOM-32 module. It is based on the ESP32 microcontroller that boasts Wifi, Bluetooth, Ethernet and Low Power support all in a single chip. (vanepp) made breadboard work, adjusted pin numbering and labels and reduced size of schematic and cleaned up pcb. This chip is 30pins long (2 x15) and 11 pins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
  Adafruit MAX98357A I2S 3W Class D Amplifier: Listen to this good news - we now have an all in one digital audio amp breakout board that works incredibly well with the Raspberry Pi! If you're looking for an easy and low cost way to get you digital sound files bumpin' then the MAX08357 I2S Amp Breakout is for you. It takes standard I2S digital audio input and, not only decodes it into analog, but also amplifies it directly into a speaker.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
  Rotary Encoder: Rotary Encoder from ALPSec11e with switch. This version has an alternate (which has been used in boards) pcb footprint from @opera_night in the forums. It is probably the best one to start from to see if you part matches.
